// Logisim project Todo.circ as structural Verilog
module rv32i (
  input  instr,
  input  ReadData,
  input  clk,
  output WE,
  output pc,
  output address,
  output WriteData
);

  wire adder_1_sal, adder_2_sal, alu_1_zero, mult2_1_sal, mult2_2_sal, mult2_3_sal, mult4_1_sal,
       register_file_1_rd1, sext_1_immext, unidad_de_control_1_alucontrol, unidad_de_control_1_alusrc,
       unidad_de_control_1_branch, unidad_de_control_1_immsrc, unidad_de_control_1_jump,
       unidad_de_control_1_regwrite, unidad_de_control_1_ressrc;

  mult2 mult2_1 (.e1(1'b0), .e2(sext_1_immext), .sal(mult2_1_sal), .sel(unidad_de_control_1_branch));
  Adder adder_1 (.A(mult2_1_sal), .B(pc), .sal(adder_1_sal));
  Adder adder_2 (.A(sext_1_immext), .B(pc), .sal(adder_2_sal));
  mult2 mult2_2 (.e1(adder_1_sal), .e2(adder_2_sal), .sal(mult2_2_sal), .sel(unidad_de_control_1_jump));
  PC pc_1 (.PCNext(mult2_2_sal), .PC(pc));
  Unidad_de_Control unidad_de_control_1 (
    .op(instr), .funct3(instr), .funct7(instr), .Zero(alu_1_zero), .Branch(unidad_de_control_1_branch),
    .ResSrc(unidad_de_control_1_ressrc), .MemWrite(WE), .ALUControl(unidad_de_control_1_alucontrol),
    .ALUSrc(unidad_de_control_1_alusrc), .ImmSrc(unidad_de_control_1_immsrc),
    .RegWrite(unidad_de_control_1_regwrite), .Jump(unidad_de_control_1_jump));
  Register_File register_file_1 (
    .WE3(unidad_de_control_1_regwrite), .A1(instr), .RD1(register_file_1_rd1), .A2(instr), .RD2(WriteData),
    .A3(instr), .WD3(mult4_1_sal));
  SExt sext_1 (.Instr(instr), .ImmExt(sext_1_immext), .ImmSrc(unidad_de_control_1_immsrc));
  mult2 mult2_3 (.e1(WriteData), .e2(sext_1_immext), .sal(mult2_3_sal), .sel(unidad_de_control_1_alusrc));
  ALU alu_1 (
    .SrcA(register_file_1_rd1), .SrcB(mult2_3_sal), .ALURes(address),
    .ALUSrc(unidad_de_control_1_alucontrol), .Zero(alu_1_zero));
  mult4 mult4_1 (
    .e1(address), .e2(ReadData), .e3(adder_1_sal), .sal(mult4_1_sal), .sel(unidad_de_control_1_ressrc));  // open: e4

  // Notes on the sheet:
  //   Branch
  //   4
  //   Imm
  //   AddSrc
  //   PC
  //   Imm
  //   PC
  //   PCNext
  //   PCJump
  //   Jump
  //   PC
  //   k+1
  //   PC
  //   Branch
  //   Jump
  //   ResSrc
  //   MemWrite
  //   ALUControl
  //   ALUSrc
  //   ImmSrc
  //   RegWrite
  //   Result
endmodule

module Instruction_Memory (
  input  PC,
  output Instr
);


  assign Instr = PC;
endmodule

module PC (
  input  PCNext,
  output PC
);


  assign PC = PCNext;
endmodule

module Adder (
  input  A,
  input  B,
  output sal
);
endmodule

module Register_File (
  input  WE3,
  input  A1,
  input  A2,
  input  A3,
  input  WD3,
  output RD1,
  output RD2
);
endmodule

module SExt (
  input  ImmSrc,
  input  Instr,
  output ImmExt
);
endmodule

module ALU (
  input  ALUSrc,
  input  SrcA,
  input  SrcB,
  output Zero,
  output ALURes
);
endmodule

module Data_Memory (
  input  WE,
  input  A,
  input  WD,
  output ReadData
);
endmodule

module Unidad_de_Control (
  input  op,
  input  funct3,
  input  funct7,
  input  Zero,
  output Branch,
  output Jump,
  output ResSrc,
  output MemWrite,
  output ALUControl,
  output ALUSrc,
  output ImmSrc,
  output RegWrite
);
endmodule

module mult2 (
  input  sel,
  input  e1,
  input  e2,
  output sal
);
endmodule

module mult4 (
  input  sel,
  input  e1,
  input  e2,
  input  e3,
  input  e4,
  output sal
);
endmodule

module Top (
  input  clk,
  input  Rx,
  output Tx
);

  wire rv32i_1_p2, rv32i_1_p3, rv32i_1_p4, rv32i_1_p5, rv32i_1_p6, rv32i_1_p7;

  // rv32i rv32i_1: pin names not known; wires that end beside it: clk, rv32i_1_p2, rv32i_1_p3, rv32i_1_p4, rv32i_1_p5, rv32i_1_p6, rv32i_1_p7
  Mem mem_1 (
    .Pc(rv32i_1_p3), .Instr(rv32i_1_p2), .WE(rv32i_1_p4), .Addres(rv32i_1_p5), .writeData(rv32i_1_p6),
    .readData(rv32i_1_p7), .clk(clk), .Rx(Rx), .Tx(Tx));

  // Notes on the sheet:
  //   Memory
endmodule

module Mem (
  input  Pc,
  input  WE,
  input  Addres,
  input  writeData,
  input  Rx,
  input  clk,
  output Instr,
  output readData,
  output Tx
);

  wire data_memory_1_readdata, data_memory_2_readdata, mmu_1_address_2, mmu_1_blockselector, mmu_1_wedata,
       mmu_1_wemmio, mmu_1_westack, uart_1_p7;

  Instruction_Memory instruction_memory_1 (.PC(Pc), .Instr(Instr));
  MMU mmu_1 (
    .address(Addres), .we(WE), .blockSelector(mmu_1_blockselector), .weMMIO(mmu_1_wemmio),
    .weStack(mmu_1_westack), .weData(mmu_1_wedata), .address_2(mmu_1_address_2));
  Data_Memory data_memory_1 (.A(mmu_1_address_2), .WD(writeData), .ReadData(data_memory_1_readdata), .WE(mmu_1_wedata));
  Data_Memory data_memory_2 (
    .A(mmu_1_address_2), .WD(writeData), .ReadData(data_memory_2_readdata), .WE(mmu_1_westack));
  // UART uart_1: pin names not known; wires that end beside it: mmu_1_address_2, writeData, Rx, clk, mmu_1_wemmio, Tx, uart_1_p7
  mult4 mult4_1 (
    .e1(data_memory_1_readdata), .e2(data_memory_2_readdata), .e3(uart_1_p7), .sal(readData),
    .sel(mmu_1_blockselector));  // open: e4

  // Notes on the sheet:
  //   Data
  //   Stack
  //   readData
endmodule

module MMU (
  input  address,
  input  we,
  output blockSelector,
  output weMMIO,
  output weStack,
  output weData,
  output address_2
);
endmodule

module UART (
  input  Rx,
  input  address,
  input  clk,
  input  w_data,
  input  we,
  output r_data,
  output Tx
);

  wire baud_rate_generator_1_out_2, converter_1_r_8bits_2, rbuffer_1_r_data, receiver_1_dout,
       receiver_1_rx_done_tick, tbuffer_1_full, tbuffer_1_r_data, transmitter_1_tx_done_tick;

  Baud_Rate_Generator baud_rate_generator_1 (.clk(clk), .out_2(baud_rate_generator_1_out_2));
  Receiver receiver_1 (
    .s_tick(baud_rate_generator_1_out_2), .dout(receiver_1_dout), .rx_done_tick(receiver_1_rx_done_tick),
    .Rx(Rx));
  Transmitter transmitter_1 (
    .in_1(baud_rate_generator_1_out_2), .din(tbuffer_1_r_data), .tx_done_tick(transmitter_1_tx_done_tick),
    .tx_start(tbuffer_1_full), .Tx(Tx));
  RBuffer rbuffer_1 (
    .w_data(receiver_1_dout), .wr(receiver_1_rx_done_tick), .A(address), .r_data(rbuffer_1_r_data));  // open: full
  TBuffer tbuffer_1 (
    .w_data(converter_1_r_8bits_2), .rd(transmitter_1_tx_done_tick), .wr(we), .r_data(tbuffer_1_r_data),
    .full(tbuffer_1_full), .A(address));
  Converter converter_1 (
    .w_8bits(rbuffer_1_r_data), .r_8bits_2(converter_1_r_8bits_2), .r_32bits(r_data), .r_8bits(w_data));

  // Notes on the sheet:
  //   tx
endmodule

module Receiver (
  input  Rx,
  input  s_tick,
  output dout,
  output rx_done_tick
);
endmodule

module Transmitter (
  input  in_1,
  input  din,
  input  tx_start,
  output Tx,
  output tx_done_tick
);
endmodule

module Baud_Rate_Generator (
  input  clk,
  output out_2
);
endmodule

module RBuffer (
  input  w_data,
  input  wr,
  input  A,
  output r_data,
  output full
);
endmodule

module TBuffer (
  input  w_data,
  input  rd,
  input  wr,
  input  A,
  output r_data,
  output full
);
endmodule

module Converter (
  input  w_8bits,
  input  r_8bits,
  output r_32bits,
  output r_8bits_2
);
endmodule
